# Fritzing sketch Arduino433MHzTransmitter (saved by Fritzing 1.0.1rc)

parts:
  U1 = FS1000A - 433Mhz RF Transmitter [package=THT]
  Part1 = Arduino Uno (Rev3) - ICSP

nets:
  N1: U1.DATA, Part1.D2
  VCC: U1.VCC, Part1.5V
  GND: U1.GND, Part1.GND

custom parts:
  FS1000A - 433Mhz RF Transmitter: This is 433Mhz RF transmitter with receiver kit for Arduino ARM MCU wireless Application environment: Remote control switch, receiver module, motorcycles, automobile anti-theft products, home security products, electric doors, shutter doors, windows, remote control socket, remote control LED, remote audio remote control electric doors, garage door remote control, remote control retractable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
