# Fritzing sketch ArduinoReceiver433 (saved by Fritzing 1.0.1rc)

parts:
  Part1 = Arduino Uno (Rev3) - ICSP
  U1 = XD-RF-5V [package=THT]

nets:
  N1: Part1.D2, U1.DATA
  5V: Part1.5V, U1.VCC
  GND: Part1.GND, U1.GND

custom parts:
  XD-RF-5V: This is 433Mhz RF transmitter with receiver kit for Arduino ARM MCU wireless Application environment: Remote control switch, receiver module, motorcycles, automobile anti-theft products, home security products, electric doors, shutter doors, windows, remote control socket, remote control LED, remote audio remote control electric doors, garage door remote control, remote control retractable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
