# Fritzing sketch ArduinoUNO_Rev3_ProtoShield (saved by Fritzing 0.9.3b)

parts:
  Bauteil1 = Adafruit Proto Shield for Arduino Kit - v.5
  U1 = FS1000A - 433Mhz RF Transmitter [package=THT]
  TRS1 = Audio Jack (TRS) 3.5mm [package="4Ucon 08780 [THT]"]
  R1 = Resistor [tolerance=±5% resistance=4.7k package="2512 [SMD]"]
  Bauteil2 = Passive Buzzer
  Bauteil3 = Arduino Uno (Rev3) - ICSP  # not connected
  Bauteil4 = DeuLigne 1.1 - The Snootlab's LCD shield for Arduino  # not connected

nets:
  GND: Bauteil1.GND, Bauteil1.N$80, Bauteil1.N$162, U1.GND, TRS1.Sleeve, Bauteil2.GND
  N1: Bauteil1.D13, Bauteil1.N$106, R1.Pin_0
  N2: Bauteil1.D12, Bauteil1.P$6#188, Bauteil2.S
  N3: Bauteil1.D11, Bauteil1.N$198, U1.DATA
  +5V: Bauteil1.+5V, Bauteil1.N$143, Bauteil1.N$270, U1.VCC
  N4: Bauteil1.P$6#132, U1.Antenna
  N5: Bauteil1.P$6#168, Bauteil2.NC
  N6: Bauteil1.N$38, Bauteil1.N$39, Bauteil1.N$104, TRS1.Ring
  N7: Bauteil1.N$49, Bauteil1.N$218, Bauteil1.N$219, TRS1.Tip, R1.Pin_1

custom parts:
  Adafruit Proto Shield for Arduino Kit - v.5: Arduino prototyping shield designed by Adafruit Industries
  FS1000A - 433Mhz RF Transmitter: This is 433Mhz RF transmitter with receiver kit for Arduino ARM MCU wireless Application environment: Remote control switch, receiver module, motorcycles, automobile anti-theft products, home security products, electric doors, shutter doors, windows, remote control socket, remote control LED, remote audio remote control electric doors, garage door remote control, remote control retractable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
